# Fritzing sketch doc (saved by Fritzing 0.9.3b)
breadboards: 1

parts:
  WeMos_D1_Mini1 = WeMos D1 Mini  # not connected
  RHT1 = Humidity and Temperature Sensor RHT03
  R1 = Resistor [tolerance=±5% resistance=10k package=THT]

nets:
  N1: RHT1.Vcc, R1.Pin_1
  N2: RHT1.Data-signal, R1.Pin_0
